// Logisim project PCUpdate.circ as structural Verilog: 3 circuits, main circuit PCUpdate
// PCUpd
module PCUpdate (
  input  [3:0] prev_segment,
  input  [3:0] offset,
  input  seg_preset,
  input  seg_clr,
  input  pc_preset,
  input  pc_clr,
  input  [7:0] ujmp_address,
  input  clk,
  input  ujmp_flag,
  output [3:0] segment,
  output [7:0] pc,
  output [15:0] Instruction
);

  wire adder4_1_p4;
  wire [3:0] n4mux2x1_1_p5, segincrement_1_inc;
  wire [6:0] undriven;
  wire [7:0] n8mux2x1_1_p2, sign_extension_out;

  Register #(.width(4), .Select("high")) seg_reg (
    .D(n4mux2x1_1_p5), .en(1'b1), .Q(segment), .clk(clk), .clr(seg_clr), .cs(1'b1), .preset(seg_preset));
  SignExt4X8 sign_extension (.in(offset), .out(sign_extension_out));
  Register #(.Select("high")) pc_reg (
    .D({undriven, 1'b0}), .en(1'b1), .Q(pc), .clk(clk), .clr(pc_clr), .cs(1'b1), .preset(pc_preset));
  SegIncrement segincrement_1 (.s(sign_extension_out[7]), .m(n8mux2x1_1_p2[7]), .inc(segincrement_1_inc));
  // Adder4 adder4_1: pin names not known; wires that end beside it: segment, segincrement_1_inc, 1'b0, adder4_1_p4
  // Adder8 adder8_1: pin names not known; wires that end beside it: sign_extension_out, {1'b0, pc[7:1]}, 1'b1
  // _4Mux2X1 4mux2x1_1: pin names not known; wires that end beside it: 1'b0, adder4_1_p4, prev_segment, ujmp_flag, n4mux2x1_1_p5
  // _8Mux2X1 8mux2x1_1: pin names not known; wires that end beside it: 1'b0, n8mux2x1_1_p2, ujmp_address, ujmp_flag
  ROM #(.addrWidth(12), .dataWidth(16), .Select("high")) Instruction_memory (
    .addr({segment, pc}), .data(Instruction), .sel(1'b1));

  // Notes on the sheet:
  //   contents of Instruction_memory (hex, n*v repeats v):
  //   10 7 1 2 3 4 5 6 7 8 9 12
endmodule

// SE4X8
module SignExt4X8 (
  input  [3:0] in,
  output [7:0] out
);


  assign out = {{5{in[3]}}, in[2:0]};
endmodule

// SegInc
module SegIncrement (
  input  s,
  input  m,
  output [3:0] inc
);

  // _7408 7408_1: pin names not known; wires that end beside it: s, m, inc[3], 1'b0, 1'b1

  assign inc[2:0] = {{2{inc[3]}}, m};
endmodule
