// Logisim project basic.circ as structural Verilog: 4 circuits, main circuit main
module main (
  input  [3:0] A,
  input  [3:0] B,
  output [3:0] out_3
);

  // _7402 7402_1: pin names not known; wires that end beside it: out_3[0], A[0], B[0], out_3[1], A[1], B[1], 1'b0, 1'b1, out_3[3], B[3], A[3], out_3[2], B[2], A[2]
endmodule

module mux (
  input  [1:0] I0,
  input  [1:0] I1,
  input  [1:0] I2,
  input  [1:0] I3,
  input  [1:0] S,
  output [1:0] R
);

  // _74153 74153_1: pin names not known; wires that end beside it: 1'b0, S[0], I3[0], I2[0], I1[0], I0[0], R[0], 1'b0, 1'b1, 1'b0, S[1], I3[1], I2[1], I1[1], I0[1], R[1]
endmodule

module dec (
  input  [2:0] in_1,
  output [7:0] out_2
);

  // _74238 74238_1: pin names not known; wires that end beside it: in_1[0], in_1[1], in_1[2], 1'b0, 1'b0, 1'b1, out_2[7], 1'b0, 1'b1, out_2[0], out_2[1], out_2[2], out_2[3], out_2[4], out_2[5], out_2[6]
endmodule

module adder (
  input  CIN,
  input  [3:0] A,
  input  [3:0] B,
  input  CIN_2,
  input  [3:0] A_2,
  input  [3:0] B_2,
  output [3:0] S,
  output [3:0] S_2
);

  wire n7483_1_p11, n7483_2_p11;

  // _7483 7483_1: pin names not known; wires that end beside it: A[3], S[2], A[2], B[2], 1'b1, S[1], B[1], A[1], B[3], S[3], n7483_1_p11, CIN, 1'b0, B[0], A[0], S[0], n7483_1_p11
  // _7483 7483_2: pin names not known; wires that end beside it: A_2[3], S_2[2], A_2[2], B_2[2], 1'b1, S_2[1], B_2[1], A_2[1], B_2[3], S_2[3], n7483_2_p11, CIN_2, 1'b0, B_2[0], A_2[0], S_2[0], n7483_2_p11
endmodule
